// Logisim project Logisim-152-246.circ as structural Verilog: 2 circuits, main circuit 0-99 Counter
module _0_99_Counter (
);

  wire and_1_out, and_2_out, and_3_out, and_4_out, and_5_out, and_6_out, and_7_out, and_8_out, clock_1_out,
       j_k_ff_1_q, j_k_ff_2_q, j_k_ff_3_q, j_k_ff_4_q, j_k_ff_5_q, j_k_ff_6_q, j_k_ff_7_q, j_k_ff_7_qn,
       j_k_ff_8_q, j_k_ff_8_qn, n7_segment_decoder_1_a, n7_segment_decoder_1_b_2, n7_segment_decoder_1_c_2,
       n7_segment_decoder_1_d_2, n7_segment_decoder_1_e, n7_segment_decoder_1_f, n7_segment_decoder_1_g,
       n7_segment_decoder_2_a, n7_segment_decoder_2_b_2, n7_segment_decoder_2_c_2, n7_segment_decoder_2_d_2,
       n7_segment_decoder_2_e, n7_segment_decoder_2_f, n7_segment_decoder_2_g, or_1_out, or_2_out;

  Clock clock_1 (.out(clock_1_out));
  J_K_Flip_Flop j_k_ff_1 (.J(1'b1), .clk(clock_1_out), .K(1'b1), .Q(j_k_ff_1_q));  // open: Qn, preset, en, reset
  and and_1 (and_1_out, j_k_ff_1_q, j_k_ff_7_qn);
  J_K_Flip_Flop j_k_ff_2 (.J(1'b1), .clk(j_k_ff_7_qn), .K(1'b1), .Q(j_k_ff_2_q));  // open: Qn, preset, en, reset
  J_K_Flip_Flop j_k_ff_3 (
    .J(and_1_out), .clk(clock_1_out), .K(and_1_out), .Q(j_k_ff_3_q));  // open: Qn, preset, en, reset
  and and_2 (and_2_out, j_k_ff_2_q, j_k_ff_8_qn);
  and and_3 (and_3_out, j_k_ff_1_q, j_k_ff_3_q);
  J_K_Flip_Flop j_k_ff_4 (
    .J(and_3_out), .clk(clock_1_out), .K(and_3_out), .Q(j_k_ff_4_q));  // open: Qn, preset, en, reset
  J_K_Flip_Flop j_k_ff_5 (
    .J(and_2_out), .clk(j_k_ff_7_qn), .K(and_2_out), .Q(j_k_ff_5_q));  // open: Qn, preset, en, reset
  and and_4 (and_4_out, j_k_ff_7_q, j_k_ff_1_q);
  and and_5 (and_5_out, and_3_out, j_k_ff_4_q);
  and and_6 (and_6_out, j_k_ff_2_q, j_k_ff_5_q);
  or or_1 (or_1_out, and_4_out, and_5_out);
  and and_7 (and_7_out, j_k_ff_8_q, j_k_ff_2_q);
  and and_8 (and_8_out, and_6_out, j_k_ff_6_q);
  J_K_Flip_Flop j_k_ff_6 (
    .J(and_6_out), .clk(j_k_ff_7_qn), .K(and_6_out), .Q(j_k_ff_6_q));  // open: Qn, preset, en, reset
  _7_Segment_Decoder u_7_segment_decoder_1 (
    .a(n7_segment_decoder_1_a), .b_2(n7_segment_decoder_1_b_2), .c_2(n7_segment_decoder_1_c_2),
    .d_2(n7_segment_decoder_1_d_2), .e(n7_segment_decoder_1_e), .f(n7_segment_decoder_1_f),
    .g(n7_segment_decoder_1_g), .A_msb(j_k_ff_8_q), .B(j_k_ff_6_q), .C(j_k_ff_5_q), .D(j_k_ff_2_q));
  J_K_Flip_Flop j_k_ff_7 (
    .J(or_1_out), .clk(clock_1_out), .K(or_1_out), .Q(j_k_ff_7_q), .Qn(j_k_ff_7_qn));  // open: preset, en, reset
  or or_2 (or_2_out, and_7_out, and_8_out);
  _7_Segment_Decoder u_7_segment_decoder_2 (
    .a(n7_segment_decoder_2_a), .b_2(n7_segment_decoder_2_b_2), .c_2(n7_segment_decoder_2_c_2),
    .d_2(n7_segment_decoder_2_d_2), .e(n7_segment_decoder_2_e), .f(n7_segment_decoder_2_f),
    .g(n7_segment_decoder_2_g), .A_msb(j_k_ff_7_q), .B(j_k_ff_4_q), .C(j_k_ff_3_q), .D(j_k_ff_1_q));
  J_K_Flip_Flop j_k_ff_8 (
    .J(or_2_out), .clk(j_k_ff_7_qn), .K(or_2_out), .Q(j_k_ff_8_q), .Qn(j_k_ff_8_qn));  // open: preset, en, reset
  _7_Segment_Display u_7_segment_display_1 (
    .g(n7_segment_decoder_1_g), .f(n7_segment_decoder_1_f), .a(n7_segment_decoder_1_a),
    .b(n7_segment_decoder_1_b_2), .e(n7_segment_decoder_1_e), .d(n7_segment_decoder_1_d_2),
    .c(n7_segment_decoder_1_c_2));  // open: dp
  _7_Segment_Display u_7_segment_display_2 (
    .g(n7_segment_decoder_2_g), .f(n7_segment_decoder_2_f), .a(n7_segment_decoder_2_a),
    .b(n7_segment_decoder_2_b_2), .e(n7_segment_decoder_2_e), .d(n7_segment_decoder_2_d_2),
    .c(n7_segment_decoder_2_c_2));  // open: dp

  // Notes on the sheet:
  //   Input 
  //   PROJECT :-
  //   0-99 COUNTER
  //   7-Segment
  //   Decoder
  //   7-Segment
  //   Decoder
  //   Team Members:-
  //   Vichitr-16CO152
  //   Shashank Kumar-16CO246
endmodule

module _7_Segment_Decoder (
  input  A_msb,
  input  B,
  input  C,
  input  D,
  output a,
  output b_2,
  output c_2,
  output d_2,
  output e,
  output f,
  output g
);

  wire and_1_out, and_2_out, and_3_out, and_4_out, and_5_out, and_6_out, and_7_out, and_8_out, and_9_out,
       not_1_out, not_2_out, not_3_out;

  not not_1 (not_1_out, B);
  not not_2 (not_2_out, C);
  not not_3 (not_3_out, D);
  and and_1 (and_1_out, B, D);
  and and_2 (and_2_out, not_1_out, not_3_out);
  and and_3 (and_3_out, C, D);
  and and_4 (and_4_out, not_2_out, not_3_out);
  and and_5 (and_5_out, C, not_3_out);
  and and_6 (and_6_out, not_1_out, C);
  and and_7 (and_7_out, B, not_2_out);
  and and_8 (and_8_out, B, not_3_out);
  and and_9 (and_9_out, D, and_7_out);
  or or_1 (a, and_1_out, and_2_out, A_msb, C);
  or or_2 (b_2, and_3_out, and_4_out, not_1_out);
  or or_3 (c_2, B, not_2_out, D);
  or or_4 (d_2, and_2_out, A_msb, and_5_out, and_6_out, and_9_out);
  or or_5 (e, and_2_out, and_5_out);
  or or_6 (f, and_4_out, and_8_out, and_7_out, A_msb);
  or or_7 (g, and_5_out, and_7_out, and_6_out, A_msb);

  // Notes on the sheet:
  //   7-Segment Decoder
endmodule
